// Logisim project CPU_Control.circ as structural Verilog
module MemRead (
  input  [3:0] in_1,
  output out_2
);

  wire not_1_out, not_2_out, not_3_out;

  not not_1 (not_1_out, in_1[1]);
  not not_2 (not_2_out, in_1[2]);
  not not_3 (not_3_out, in_1[3]);
  and and_1 (out_2, in_1[0], not_1_out, not_2_out, not_3_out);
endmodule

module MemtoReg (
  input  [3:0] in_1,
  output out_2
);

  wire not_1_out, not_2_out, not_3_out;

  not not_1 (not_1_out, in_1[1]);
  not not_2 (not_2_out, in_1[2]);
  not not_3 (not_3_out, in_1[3]);
  and and_1 (out_2, in_1[0], not_1_out, not_2_out, not_3_out);
endmodule

module MemWrite (
  input  [3:0] in_1,
  output out_2
);

  wire not_1_out, not_2_out;

  not not_1 (not_1_out, in_1[1]);
  not not_2 (not_2_out, in_1[3]);
  and and_1 (out_2, in_1[0], not_1_out, in_1[2], not_2_out);
endmodule

module Clock_Stop_8053a739 (
  input  [3:0] in_1,
  output out_2
);

  and and_1 (out_2, in_1[0], in_1[1], in_1[2], in_1[3]);
endmodule

module Write_ra_f61e1106 (
  input  [3:0] in_1,
  output out_2
);

  wire not_1_out;

  not not_1 (not_1_out, in_1[1]);
  and and_1 (out_2, in_1[0], not_1_out, in_1[2], in_1[3]);
endmodule

module Read_ra_849e8755 (
  input  [3:0] in_1,
  output out_2
);

  wire not_1_out;

  not not_1 (not_1_out, in_1[0]);
  and and_1 (out_2, not_1_out, in_1[1], in_1[2], in_1[3]);
endmodule

module RegWrite (
  input  [3:0] in_1,
  output out_2
);

  wire and_1_out, and_2_out, and_3_out, and_4_out;

  and and_1 (and_1_out, ~in_1[0], ~in_1[1], ~in_1[3]);  // AND_Gate
  and and_2 (and_2_out, ~in_1[3], ~in_1[2], ~in_1[1]);  // AND_Gate
  and and_3 (and_3_out, in_1[3], ~in_1[2], ~in_1[1]);  // AND_Gate
  and and_4 (and_4_out, in_1[1], ~in_1[3]);  // AND_Gate
  or or_1 (out_2, and_1_out, and_2_out, and_3_out, and_4_out);
endmodule

module Branch (
  input  [3:0] in_1,
  output out_2
);

  wire and_1_out, and_2_out, and_3_out, and_4_out;

  and and_1 (and_1_out, in_1[2], ~in_1[1], ~in_1[0]);  // AND_Gate
  and and_2 (and_2_out, ~in_1[1], in_1[2], in_1[3]);  // AND_Gate
  and and_3 (and_3_out, in_1[1], ~in_1[2], in_1[3]);  // AND_Gate
  and and_4 (and_4_out, ~in_1[0], in_1[1], in_1[3]);  // AND_Gate
  or or_1 (out_2, and_1_out, and_2_out, and_3_out, and_4_out);
endmodule

module ALUop1 (
  input  [3:0] in_1,
  output out_2
);

  wire and_1_out, and_2_out;

  and and_1 (and_1_out, ~in_1[0], ~in_1[1], ~in_1[2], in_1[3]);  // AND_Gate
  and and_2 (and_2_out, in_1[1], ~in_1[2], in_1[3]);  // AND_Gate
  or or_1 (out_2, and_1_out, and_2_out);
endmodule

module ALUop2 (
  input  [3:0] in_1,
  output out_2
);

  wire and_1_out, and_2_out, and_3_out;

  and and_1 (and_1_out, ~in_1[1], ~in_1[2], in_1[3]);  // AND_Gate
  and and_2 (and_2_out, ~in_1[1], ~in_1[2], ~in_1[3], in_1[0]);  // AND_Gate
  and and_3 (and_3_out, in_1[1], ~in_1[2], ~in_1[3]);  // AND_Gate
  or or_1 (out_2, and_1_out, and_2_out, and_3_out);
endmodule

module ALUSrc (
  input  [3:0] in_1,
  output out_2
);

  wire and_1_out, and_2_out, and_3_out;

  and and_1 (and_1_out, ~in_1[0], ~in_1[1], ~in_1[3]);  // AND_Gate
  and and_2 (and_2_out, in_1[3], ~in_1[2], ~in_1[1]);  // AND_Gate
  and and_3 (and_3_out, in_1[0], in_1[2], ~in_1[3]);  // AND_Gate
  or or_1 (out_2, and_1_out, and_2_out, and_3_out);
endmodule
